# Fritzing sketch Airlogger (saved by Fritzing 0.9.9b)
perfboards: 1

parts:
  M1 = DOIT Esp32 DevKit v1 (30 pins long, 11 pins width) [part_number=ESP32S-PIN30]
  BME680_Humidity_Pressure_Temperature_Sensor = Adafruit BME680 [part_number="Adafruit #3660"]
  Sensirion_SCD30_CO2_Sensor = SCD30

nets:
  3V3: M1.3V3, BME680_Humidity_Pressure_Temperature_Sensor.VCC, Sensirion_SCD30_CO2_Sensor.VDD
  GND: M1.GND, BME680_Humidity_Pressure_Temperature_Sensor.GND, Sensirion_SCD30_CO2_Sensor.GND
  N1: M1.D21, BME680_Humidity_Pressure_Temperature_Sensor.SDI/SDA, Sensirion_SCD30_CO2_Sensor.RX/SDA
  N2: M1.D22, BME680_Humidity_Pressure_Temperature_Sensor.SCK/SCL, Sensirion_SCD30_CO2_Sensor.TX/SCL

custom parts:
  DOIT Esp32 DevKit v1 (30 pins long, 11 pins width): The DOIT Esp32 DevKit v1 is one of the development board created by DOIT to evaluate the ESP-WROOM-32 module. It is based on the ESP32 microcontroller that boasts Wifi, Bluetooth, Ethernet and Low Power support all in a single chip. (vanepp) made breadboard work, adjusted pin numbering and labels and reduced size of schematic and cleaned up pcb. This chip is 30pins long (2 x15) and 11 pins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
  SCD30: CO2 , humidity, and temperature sensor * Current consumption: 19 mA @ 1 meas. per 2 s. * Digital interface UART or I2C * Company: Sensirion - The Sensor Company Electrical specifications * average current: 19 mA * max. current: 75 mA * DC supply: 3.3 V - 5.5 V Operation conditions * temperature: 0 – 50°C * humidity: 0 – 95 %RH * sensor lifetime: 15 years CO2-sensor: * NDIR CO 2 sensor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
